// Digital circuit CPU_main.dig as structural Verilog
module CPU_main (
  input  Acc_out,
  input  ALU_out
);

  wire IR_MAR, LDA_instr, MEM_ACC, or_1_out, or_2_out, RESET_CLK, T1, T2, T3, T4, T5, T6;
  wire [2:0] COUNTER;
  wire [3:0] ADRESS, OPCODE;
  wire [7:0] Acc_q, alu_main_1_p2, PC_out, W_BUS;
  wire [15:0] CONTROL_ROM_d;

  CounterPreset PC (.en(T2), .in(W_BUS[0]), .out(PC_out[0]));  // open: C, dir, ld, clr, ovf
  ROM #(.AddrBits(7), .Bits(16)) CONTROL_ROM (.A({COUNTER, OPCODE}), .D(CONTROL_ROM_d));  // open: sel
  assign W_BUS = T1 ? PC_out : 8'bz;  // Driver driver_1
  or or_1 (or_1_out, T3, MEM_ACC);
  Counter #(.Bits(3)) u_Counter (.clr(RESET_CLK), .out(COUNTER));  // open: en, C, ovf
  // Probe on W_BUS
  ROM #(.AddrBits(8), .Bits(8)) ROM (.sel(or_1_out), .D(W_BUS));  // open: A
  Decoder #(.Selector_Bits(3)) decoder_1 (
    .sel(COUNTER), .out_0(T1), .out_1(T2), .out_2(T3), .out_3(T4), .out_4(T5), .out_5(T6));  // open: out_6, out_7
  Register #(.Bits(8)) Acc (.en(MEM_ACC), .Q(Acc_q));  // open: D, C
  Decoder #(.Selector_Bits(4)) decoder_2 (
    .sel(OPCODE), .out_0(LDA_instr));  // open: out_1, out_2, out_3, out_4, out_5, out_6, out_7, out_8, out_9, out_10, out_11, out_12, out_13, out_14, out_15
  assign W_BUS = Acc_out ? Acc_q : 8'bz;  // Driver driver_2
  Register #(.Bits(8)) IR (.D(W_BUS), .en(T3), .Q({ADRESS, OPCODE}));  // open: C
  // ALU_main alu_main_1: pin names not known; wires that end beside it: W_BUS, alu_main_1_p2
  assign W_BUS = IR_MAR ? {ADRESS, OPCODE} : 8'bz;  // Driver driver_3
  assign W_BUS = ALU_out ? alu_main_1_p2 : 8'bz;  // Driver driver_4
  Register #(.Bits(8)) B_reg (.D(W_BUS));  // open: C, en, Q
  Register #(.Bits(8)) Out_reg (.D(W_BUS));  // open: C, en, Q
  or or_2 (or_2_out, T1, IR_MAR);
  and and_1 (IR_MAR, T4, LDA_instr);
  and and_2 (MEM_ACC, T5, LDA_instr);
  and and_3 (RESET_CLK, T6, LDA_instr);
  Register #(.Bits(8)) MAR (.D(W_BUS), .en(or_2_out));  // open: C, Q
  // Pins of 1 and 8 bits meet at W_BUS
  // Pins of 1 and 8 bits meet at PC_out
endmodule
